# Fritzing sketch car_sketch (saved by Fritzing 1.0.1rc)
circuit board: 11.1455cm x 10.9907cm
breadboards: 1

parts:
  Arduino = Arduino Uno (Rev3) - ICSP
  M1 = gear-motor
  M2 = gear-motor
  M4 = gear-motor
  VCC1 = 4 x AAA Battery Mount
  HC-SR04_Sensor_1 = HC-SR04 Ultrasonic Distance Sensor
  M3 = gear-motor
  S2 = H-Bridge with L298N
  Part1 = NRF24L01+ Breakout Board  # not connected

nets:
  GND: Arduino.GND, VCC1.-, HC-SR04_Sensor_1.GND, S2.GND
  N1: Arduino.D8, S2.IN2
  N2: Arduino.D9_PWM, S2.IN1
  N3: Arduino.D10_PWM/SS, S2.ENA
  N4: Arduino.D2, HC-SR04_Sensor_1.TRIG
  N5: Arduino.D4, HC-SR04_Sensor_1.ECHO
  N6: Arduino.D5_PWM, S2.ENB
  N7: Arduino.D6_PWM, S2.IN4
  N8: Arduino.D7, S2.IN3
  VIN: Arduino.VIN, VCC1.+, HC-SR04_Sensor_1.VCC
  N9: M1.pin_1, M3.pin_1
  N10: M1.pin_2, M3.pin_2, S2.M1-01
  N11: M2.pin_1, M4.pin_1, S2.M2-02
  N12: M2.pin_2, M4.pin_2, S2.M2-01

custom parts:
  H-Bridge with L298N: h-bridge
